# Fritzing sketch TinkurCrate Wiring Diagram (saved by Fritzing 0.8.7b)

parts:
  Part1 = Arduino Ethernet Shield (Rev3)
  J1 = Infrared Proximity Sensor

nets:
  N1: Part1.A5/SCL, J1.Vout
  5V: Part1.5V, J1.Vcc
  GND: Part1.GND, J1.GND

notes:
  Data sent to Xively for storage and post processing
  Xively triggers Zappier Web Hooks when the InCrate status changes, triggering a Twitter post
